# Fritzing sketch arduino_bb_8mhz (saved by Fritzing 0.9.2b)
breadboards: 1

parts:
  U1 = atmega328 [package=dip]
  C1 = Ceramic Capacitor [capacitance=100nF package="100 mil [THT, multilayer]"]
  U2 = Voltage Regulator - 5V [package="TO220 [THT]"]
  C2 = Electrolytic Capacitor [capacitance=10µF package="100 mil [THT, electrolytic]"]
  VCC1 = Battery block 9V
  C3 = Electrolytic Capacitor [capacitance=10µF package="100 mil [THT, electrolytic]"]
  R1 = Resistor [tolerance=±5% resistance=10k package=THT]

nets:
  N1: U1.RESET, R1.Pin_0
  N2: U1.VCC, U1.AVCC, U1.AREF, C1.1, U2.output_voltage, C3.+, R1.Pin_1
  GND: U1.GND, C1.0, U2.GND, C2.-, VCC1.-, C3.-
  N3: U2.input_voltage, C2.+, VCC1.+
